// Logisim project SRM1.circ as structural Verilog: 9 circuits, main circuit SRM1
module BCDADDER (
  input  Cin,
  input  [7:0] A,
  input  [7:0] B,
  output [7:0] O,
  output Cout
);

  wire adder_1_cout, adder_2_cout, adder_3_cout, and_1_out, and_2_out, and_3_out, and_4_out, or_1_out;
  wire [2:2] or_2_out, or_3_out;
  wire [3:0] adder_1_out, adder_2_out;

  Adder #(.width(4)) adder_1 (.a(A[3:0]), .b(B[3:0]), .out(adder_1_out), .cin(Cin), .cout(adder_1_cout));
  or or_1 (or_1_out, adder_1_cout, adder_3_cout);
  Adder #(.width(4)) adder_2 (.a(A[7:4]), .b(B[7:4]), .out(adder_2_out), .cin(or_1_out), .cout(adder_2_cout));
  Adder #(.width(4)) adder_3 (
    .a(adder_1_out), .b({1'b0, {2{or_2_out[2]}}, 1'b0}), .out(O[3:0]), .cin(1'b0), .cout(adder_3_cout));
  Adder #(.width(4)) adder_4 (
    .a(adder_2_out), .b({1'b0, {2{or_3_out[2]}}, 1'b0}), .out(O[7:4]), .cin(1'b0), .cout(Cout));
  and and_1 (and_1_out, adder_1_out[2], adder_1_out[3]);
  and and_2 (and_2_out, adder_1_out[1], adder_1_out[3]);
  and and_3 (and_3_out, adder_2_out[2], adder_2_out[3]);
  and and_4 (and_4_out, adder_2_out[1], adder_2_out[3]);
  or or_2 (or_2_out[2], and_1_out, and_2_out, adder_1_cout);
  or or_3 (or_3_out[2], and_3_out, and_4_out, adder_2_cout);
endmodule

module BCDSUBTRACTOR (
  input  Bin,
  input  [7:0] A,
  input  [7:0] B,
  output [7:0] O,
  output Bout
);

  wire and_1_out, and_2_out, and_3_out, and_4_out, or_1_out, subtractor_1_bout, subtractor_2_bout,
       subtractor_3_bout;
  wire [2:2] or_2_out, or_3_out;
  wire [3:0] subtractor_1_out, subtractor_2_out;

  Subtractor #(.width(4)) subtractor_1 (
    .a(A[3:0]), .b(B[3:0]), .out(subtractor_1_out), .bin(Bin), .bout(subtractor_1_bout));
  or or_1 (or_1_out, subtractor_1_bout, subtractor_3_bout);
  Subtractor #(.width(4)) subtractor_2 (
    .a(A[7:4]), .b(B[7:4]), .out(subtractor_2_out), .bin(or_1_out), .bout(subtractor_2_bout));
  Subtractor #(.width(4)) subtractor_3 (
    .a(subtractor_1_out), .b({1'b0, {2{or_2_out[2]}}, 1'b0}), .out(O[3:0]), .bin(1'b0),
    .bout(subtractor_3_bout));
  Subtractor #(.width(4)) subtractor_4 (
    .a(subtractor_2_out), .b({1'b0, {2{or_3_out[2]}}, 1'b0}), .out(O[7:4]), .bin(1'b0), .bout(Bout));
  and and_1 (and_1_out, subtractor_1_out[2], subtractor_1_out[3]);
  and and_2 (and_2_out, subtractor_1_out[1], subtractor_1_out[3]);
  and and_3 (and_3_out, subtractor_2_out[2], subtractor_2_out[3]);
  and and_4 (and_4_out, subtractor_2_out[1], subtractor_2_out[3]);
  or or_2 (or_2_out[2], and_1_out, and_2_out, subtractor_1_bout);
  or or_3 (or_3_out[2], and_3_out, and_4_out, subtractor_2_bout);
endmodule

module ALU (
  input  BCD,
  input  Cin,
  input  [15:0] A,
  input  [15:0] B,
  input  [3:0] OP,
  output [15:0] Dout,
  output S,
  output Z,
  output Cout,
  output GT,
  output LT,
  output Overflow
);

  wire adder_1_cout, BCDAH_cout, BCDAL_cout, BCDSH_bout, BCDSL_bout, Cin_EN_out, multiplexer_3_out,
       multiplexer_5_out, OV_EN_out, subtractor_1_bout, xor_1_out;
  wire [1:0] Cout_SEL_out;
  wire [7:0] BCDAH_o, BCDAL_o, BCDSH_o, BCDSL_o;
  wire [15:0] adder_1_out, and_1_out, multiplexer_2_out, multiplexer_4_out, negator_1_out, or_1_out,
       subtractor_1_out, xor_2_out;
  wire [15:15] multiplexer_1_out;

  xor xor_1 (xor_1_out, A[15], B[15]);
  PLA #(.in_width(4), .out_width(1), .\table ("0001 1 # ADC\n0011 1 # SBB\n1000 1 # SRC")) Cin_EN (
    .in(OP), .out(Cin_EN_out));
  PLA #(.in_width(4), .\table ("0000 00 # ADD\n0001 00 # ADC\n0010 01 # SUB\n0011 01 # SBB\n0111 10 # SHR\n1000 10 # SRC\n1001 11 # ASR")) Cout_SEL (
    .in(OP), .out(Cout_SEL_out));
  Multiplexer multiplexer_1 (.in0(1'b0), .in1(Cin), .out(multiplexer_1_out[15]), .sel(Cin_EN_out));
  assign and_1_out = A & B;  // AND_Gate and_1, 16 bits wide
  assign or_1_out = A | B;  // OR_Gate or_1, 16 bits wide
  assign xor_2_out = A ^ B;  // XOR_Gate xor_2, 16 bits wide
  Adder #(.width(16)) adder_1 (.a(A), .b(B), .out(adder_1_out), .cin(multiplexer_1_out[15]), .cout(adder_1_cout));
  BCDADDER BCDAL (.A(A[7:0]), .B(B[7:0]), .Cin(multiplexer_1_out[15]), .O(BCDAL_o), .Cout(BCDAL_cout));
  BCDADDER BCDAH (.A(A[15:8]), .B(B[15:8]), .Cin(BCDAL_cout), .O(BCDAH_o), .Cout(BCDAH_cout));
  Subtractor #(.width(16)) subtractor_1 (
    .a(A), .b(B), .out(subtractor_1_out), .bin(multiplexer_1_out[15]), .bout(subtractor_1_bout));
  BCDSUBTRACTOR BCDSL (.A(A[7:0]), .B(B[7:0]), .Bin(multiplexer_1_out[15]), .Bout(BCDSL_bout), .O(BCDSL_o));
  BCDSUBTRACTOR BCDSH (.A(A[15:8]), .B(B[15:8]), .Bin(BCDSL_bout), .Bout(BCDSH_bout), .O(BCDSH_o));
  Negator #(.width(16)) negator_1 (.in(A), .out(negator_1_out));
  Comparator #(.mode("unsigned"), .width(16)) comparator_1 (.a(A), .b(B), .gt(GT), .lt(LT));  // open: eq
  Multiplexer #(.width(16)) multiplexer_2 (
    .in0(adder_1_out), .in1({BCDAH_o, BCDAL_o}), .out(multiplexer_2_out), .sel(BCD));
  Multiplexer multiplexer_3 (.in0(adder_1_cout), .in1(BCDAH_cout), .out(multiplexer_3_out), .sel(BCD));
  Multiplexer #(.width(16)) multiplexer_4 (
    .in0(subtractor_1_out), .in1({BCDSH_o, BCDSL_o}), .out(multiplexer_4_out), .sel(BCD));
  Multiplexer multiplexer_5 (.in0(subtractor_1_bout), .in1(BCDSH_bout), .out(multiplexer_5_out), .sel(BCD));
  PLA #(.in_width(4), .out_width(1), .\table ("0000 1 # ADD\n0001 1 # ADC\n0010 1 # SUB\n0011 1 # SBB")) OV_EN (
    .in(OP), .out(OV_EN_out));
  Multiplexer #(.select(4), .width(16)) multiplexer_6 (
    .in0(multiplexer_2_out), .in1(multiplexer_2_out), .in2(multiplexer_4_out), .in3(multiplexer_4_out),
    .in4(and_1_out), .in5(or_1_out), .in6(xor_2_out), .in7({multiplexer_1_out[15], A[15:1]}),
    .in8({multiplexer_1_out[15], A[15:1]}), .in9({{2{A[15]}}, A[14:1]}), .in10({A[0], A[15:1]}),
    .in11({A[14:0], A[15]}), .in12(negator_1_out), .in13({16{1'b0}}), .in14({16{1'b0}}), .in15({16{1'b0}}),
    .out(Dout), .sel(OP));
  Multiplexer #(.select(2)) multiplexer_7 (
    .in0(multiplexer_3_out), .in1(multiplexer_5_out), .in2(A[0]), .in3(A[0]), .out(Cout), .sel(Cout_SEL_out));
  nor nor_1 (Z, Dout[15], Dout[14], Dout[13], Dout[12], Dout[11], Dout[10], Dout[9], Dout[8], Dout[7], Dout[6], Dout[5], Dout[4], Dout[3], Dout[2], Dout[1], Dout[0]);
  and and_2 (Overflow, xor_1_out, OV_EN_out);

  assign S = Dout[15];
endmodule

module SRM1 (
  input  [7:0] DLO,
  input  [7:0] DHO,
  input  RES,
  input  RDY,
  input  IRQ,
  input  NMI,
  output [19:0] AB,
  output [7:0] DHI,
  output [7:0] DLI,
  output RW,
  output WS,
  output ML,
  output Interrupt_Fetch
);

  wire ALU_A_SEL, and_1_out, and_2_out, and_3_out, and_9_out, and_10_out, bitselector_1_out, BS, C_sel,
       clock_1_out, clock_2_out, clock_3_out, clock_4_out, clock_5_out, Enable, IN_sel, INT_Sel, LB, LPCE,
       ML_EN_out, OP_Sel, or_1_out, or_2_out, PC_E, PC_L, PC_R, RF_WE, RMC, S_IR, s_r_ff_1_q, s_r_ff_2_q,
       s_r_ff_3_q, STAT_BIT_WE, STAT_R, STAT_S, STAT_WE, Temp_Address_Holder_p1, Temp_Address_Holder_p2,
       WS_EN_out, xor_1_out, xor_2_out;
  wire [1:0] ALU_B_SEL, Secondary_Microcode_out;
  wire [2:0] AB_Sel, DB_Sel;
  wire [3:0] counter_1_q, Instruction_Encoder_out, multiplexer_5_out, multiplexer_9_out, multiplexer_10_out,
       multiplexer_13_out, multiplexer_14_out;
  wire [3:1] Microcode_out;
  wire [5:0] A_L_U_z;
  wire [7:0] SR;
  wire [15:0] A, ALU_OUT, B, bit_extender_1_out, bit_extender_2_out, BX, C, DB, IB, multiplexer_7_out,
       multiplexer_11_out, multiplexer_12_out, SX;
  wire [19:0] adder_1_out, bit_extender_3_out, multiplexer_6_out, multiplexer_8_out, PC_Dout, SP, TA;
  wire [31:0] IR;

  xor xor_1 (xor_1_out, 1'b1, RES);
  and and_1 (and_1_out, IR[28], ~IR[29], ~IR[30], ~IR[31]);  // AND_Gate
  and and_2 (and_2_out, IR[28], IR[29], IR[30], IR[31]);
  S_R_Flip_Flop s_r_ff_1 (
    .S(xor_1_out), .R(RES), .clk(clock_1_out), .Q(s_r_ff_1_q), .reset(1'b0), .Qn(PC_R), .preset(1'b0));
  Clock clock_1 (.out(clock_1_out));
  and and_3 (and_3_out, IRQ, SR[7]);
  Clock clock_2 (.out(clock_2_out));
  Clock clock_3 (.out(clock_3_out));
  assign bit_extender_1_out = {{8{1'b0}}, DHO};  // Bit_Extender bit_extender_1
  Multiplexer #(.width(16)) multiplexer_1 (.in0({IB[7:0], IB[15:8]}), .in1(IB), .out({DLI, DHI}), .sel(BS));
  S_R_Flip_Flop s_r_ff_2 (
    .S(and_3_out), .R(and_1_out), .clk(clock_2_out), .Q(s_r_ff_2_q), .reset(1'b0), .preset(1'b0));  // open: Qn
  S_R_Flip_Flop s_r_ff_3 (
    .S(NMI), .R(and_2_out), .clk(clock_3_out), .Q(s_r_ff_3_q), .reset(1'b0), .preset(1'b0));  // open: Qn
  Multiplexer #(.width(16)) multiplexer_2 (.in0({DHO, DLO}), .in1(bit_extender_1_out), .out(DB), .sel(LB));
  and and_4 (Enable, s_r_ff_1_q, RDY);
  Multiplexer #(.select(3), .width(20)) multiplexer_3 (
    .in0(PC_Dout), .in1(multiplexer_8_out), .in2(multiplexer_6_out), .in3(TA), .in4(SP), .out(AB),
    .sel(AB_Sel));  // open: in5, in6, in7
  assign bit_extender_2_out = {{8{1'b0}}, SR};  // Bit_Extender bit_extender_2
  or or_1 (or_1_out, s_r_ff_3_q, s_r_ff_2_q);
  and and_5 (Interrupt_Fetch, or_1_out, S_IR);
  Multiplexer #(.select(3), .width(16)) multiplexer_4 (
    .in0(DB), .in1(ALU_OUT), .in2(bit_extender_2_out), .in3(C), .in4(PC_Dout[15:0]),
    .in5({{12{1'b0}}, PC_Dout[19:16]}), .out(IB), .sel(DB_Sel));  // open: in6, in7
  Multiplexer #(.width(4)) multiplexer_5 (.in0(4'b0001), .in1(4'b1111), .out(multiplexer_5_out), .sel(s_r_ff_3_q));
  or or_2 (or_2_out, s_r_ff_2_q, s_r_ff_3_q);
  Multiplexer #(.width(20)) multiplexer_6 (.in0(20'hffff8), .in1(20'hffffc), .out(multiplexer_6_out), .sel(INT_Sel));
  Multiplexer #(.width(16)) multiplexer_7 (
    .in0({DHO, DLO}), .in1({multiplexer_5_out, {12{1'b0}}}), .out(multiplexer_7_out), .sel(or_2_out));
  and and_6 (BS, LB, WS_EN_out);
  not not_1 (WS, BS);
  Multiplexer #(.select(2), .width(20)) multiplexer_8 (
    .in0(IR[19:0]), .in1(adder_1_out), .in2({IR[19:16], B}), .in3({A[3:0], B}), .out(multiplexer_8_out),
    .sel(IR[25:24]));
  Clock clock_4 (.out(clock_4_out));
  PLA #(.in_width(4), .out_width(1), .\table ("0100 1 # STR")) WS_EN (.in(IR[31:28]), .out(WS_EN_out));
  // Shift_Register #(.length(2), .width(16)) IR: pin names not known; wires that end beside it: 1'b0, 1'b0, S_IR, clock_4_out, multiplexer_7_out, {16{1'b0}}
  PLA #(.in_width(4), .out_width(4), .\table ("0000 0000 # NOP\n0001 0001 # BRK\n1111 0001 # NMI\n0010 0010 # ALU\n0011 0010 # ALI\n0100 0011 # STR\n0101 0100 # LOD\n0110 0101 # PSH\n0111 0110 # POP\n1000 0111 # JMP\n1001 0111 # JIF\n1010 1000 # CAL\n1011 1001 # RET\n1100 1010 # SF\n1101 1010 # CF\n1110 1011 # RTI")) Instruction_Encoder (
    .in(IR[31:28]), .out(Instruction_Encoder_out));
  Counter #(.max('hf), .width(4)) counter_1 (
    .load(RMC), .D(4'b0000), .count(Enable), .Q(counter_1_q), .up(1'b1), .clk(clock_5_out), .clr(1'b0));  // open: carry
  Clock clock_5 (.out(clock_5_out));
  or or_3 (ML, WS_EN_out, ML_EN_out, S_IR);
  PLA #(.in_width(4), .out_width(1), .\table ("0101 1 # LOD\n0110 1 # PSH\n0111 1 # POP\n1000 1 # JMP\n1001 1 # JIF\n1010 1 # CAL\n1011 1 # RET\n1110 1 # RTI\n1111 1 # NMI\n0001 1 # BRK")) ML_EN (
    .in(IR[31:28]), .out(ML_EN_out));
  assign bit_extender_3_out = {{4{1'b0}}, BX};  // Bit_Extender bit_extender_3
  Multiplexer #(.width(4)) multiplexer_9 (
    .in0(4'b0000), .in1(Instruction_Encoder_out), .out(multiplexer_9_out), .sel(Enable));
  Adder #(.width(20)) adder_1 (.a(IR[19:0]), .b(bit_extender_3_out), .out(adder_1_out), .cin(1'b0));  // open: cout
  Multiplexer #(.width(4)) multiplexer_10 (.in0(IR[23:20]), .in1(4'b0111), .out(multiplexer_10_out), .sel(C_sel));
  PLA #(.in_width(8), .out_width(15), .\table ("0000xxxx 000000000000110 # FETCH\n0001xxxx 000000000000110 # FETCH\n00100000 000000000000001 # NOP\n00100010 000001001010001 # ALU/ALI\n00100011 011011100000001 # STR\n00100100 001000000010001 # LOD\n00110101 100011100000001 # PSH\n00100101 000001000110000 # PSH\n00100110 100000000010000 # POP\n00110110 000001000110001 # POP\n00100111 001000000001101 # JMP/JIF\n00101000 000001000110000 # CAL\n00111000 100100100000000 # CAL\n01001000 000001000110000 # CAL\n01011000 100101100000000 # CAL\n01101000 000000000001101 # CAL\n00101001 100001000110000 # RET\n00111001 100001000110000 # RET\n01001001 011000000001101 # RET\n00101010 000000010000001 # SF/CF\n00100001 000001000110000 # BRK/NMI\n00110001 100100100000000 # BRK/NMI\n01000001 000001000110000 # BRK/NMI\n01010001 100101100000000 # BRK/NMI\n01100001 000001000110000 # BRK/NMI\n01110001 100010100000000 # BRK/NMI\n10000001 010000000001101 # BRK/NMI\n00101011 100000001000000 # RTI\n00111011 100001000110000 # RTI\n01001011 100001000110000 # RTI\n01011011 100001000110000 # RTI\n01101011 011000000001101 # RTI")) Microcode (
    .in({counter_1_q, multiplexer_9_out}),
    .out({AB_Sel, DB_Sel, RW, STAT_BIT_WE, STAT_WE, C_sel, RF_WE, Microcode_out, RMC}));
  PC Program_Counter (.Din(AB), .R(PC_R), .L(PC_L), .E(PC_E), .Dout(PC_Dout));
  REG_FILE REG_Bank (
    .WE(RF_WE), .Din(IB), .C(multiplexer_10_out), .A(IR[23:20]), .B(IR[19:16]), .Bout(B), .Cout(C), .Aout(A),
    .BX_Out(BX), .LB(LB), .SX_Out(SX), .SP(SP));
  // Shift_Register #(.length(2), .width(16)) Temp_Address_Holder: pin names not known; wires that end beside it: Temp_Address_Holder_p1, Temp_Address_Holder_p2, DB, {16{1'b0}}, {16{1'b0}}
  not not_2 (Temp_Address_Holder_p1, PC_L);
  Clock clock_6 (.out(Temp_Address_Holder_p2));
  and and_7 (PC_L, Microcode_out[3], LPCE);
  Multiplexer #(.select(2), .width(16)) multiplexer_11 (
    .in0(B), .in1(IR[15:0]), .in2(16'h2), .in3(16'hfffe), .out(multiplexer_11_out), .sel(ALU_B_SEL));
  and and_8 (S_IR, Microcode_out[1], Enable);
  and and_9 (and_9_out, Enable, Microcode_out[2]);
  and and_10 (and_10_out, Microcode_out[3], ~PC_L);  // AND_Gate
  Multiplexer #(.width(16)) multiplexer_12 (.in0(A), .in1(SX), .out(multiplexer_12_out), .sel(ALU_A_SEL));
  and and_11 (PC_E, and_9_out, ~and_10_out);  // AND_Gate
  PLA #(.in_width(4), .out_width(8), .\table ("0001 11110001 # BRK\n1111 11111001 # NMI\n0011 01000100 # ALI\n0110 11110000 # PSH\n0111 10110000 # POP\n1000 00000001 # JMP\n1010 11110001 # CAL\n1011 10110001 # RET\n1100 00000010 # SF\n1101 00000000 # CF\n1110 10110001 # RTI\n0010 00000100 # ALU")) Secondary_Microcode (
    .in(multiplexer_13_out), .out({ALU_B_SEL, ALU_A_SEL, OP_Sel, INT_Sel, IN_sel, Secondary_Microcode_out}));
  Multiplexer #(.width(4)) multiplexer_13 (.in0(IR[31:28]), .in1(4'b0000), .out(multiplexer_13_out), .sel(S_IR));
  Multiplexer #(.width(4)) multiplexer_14 (.in0(IR[27:24]), .in1(4'b0000), .out(multiplexer_14_out), .sel(OP_Sel));
  ALU A_L_U (
    .Cin(SR[1]), .A(multiplexer_12_out), .B(multiplexer_11_out), .OP(multiplexer_14_out), .BCD(SR[6]),
    .Dout(ALU_OUT), .S(A_L_U_z[3]), .Cout(A_L_U_z[2]), .GT(A_L_U_z[4]), .LT(A_L_U_z[5]),
    .Overflow(A_L_U_z[1]), .Z(A_L_U_z[0]));
  Demultiplexer demultiplexer_1 (.out0(STAT_R), .out1(STAT_S), .in(STAT_BIT_WE), .sel(Secondary_Microcode_out[1]));
  BitSelector bitselector_1 (.in(SR), .out(bitselector_1_out), .sel(IR[26:24]));
  xor xor_2 (xor_2_out, bitselector_1_out, IR[27]);
  Status STAT (
    .DBin(IB[7:0]), .Fin(A_L_U_z), .WE(STAT_WE), .In_Sel(IN_sel), .Fsel(IR[22:20]), .R(STAT_R), .S(STAT_S),
    .Dout(SR));
  or or_4 (LPCE, Secondary_Microcode_out[0], xor_2_out);

  // Other names for the same wires on the sheet: M2 = RW

  // Notes on the sheet:
  //   RDY: initial=0x1
endmodule

module Status (
  input  R,
  input  S,
  input  [2:0] Fsel,
  input  [7:0] DBin,
  input  [5:0] Fin,
  input  WE,
  input  In_Sel,
  output [7:0] Dout
);

  wire and_1_out, and_2_out, and_3_out, and_4_out, and_5_out, and_6_out, and_7_out, and_8_out, and_9_out,
       and_10_out, and_11_out, and_12_out, and_13_out, and_14_out, and_15_out, and_16_out, and_17_out,
       and_18_out, and_19_out, and_20_out, and_21_out, and_22_out, and_23_out, and_24_out, clock_1_out,
       clock_2_out, clock_3_out, clock_4_out, clock_5_out, clock_6_out, clock_7_out, clock_8_out,
       decoder_1_out0, decoder_1_out1, decoder_1_out2, decoder_1_out3, decoder_1_out4, decoder_1_out5,
       decoder_1_out6, decoder_1_out7;
  wire [7:0] multiplexer_1_out;

  Multiplexer #(.width(8)) multiplexer_1 (.in0(DBin), .in1({Dout[7:6], Fin}), .out(multiplexer_1_out), .sel(In_Sel));
  Decoder #(.enable("false"), .select(3)) decoder_1 (
    .out0(decoder_1_out0), .out1(decoder_1_out1), .out2(decoder_1_out2), .out3(decoder_1_out3),
    .out4(decoder_1_out4), .out5(decoder_1_out5), .out6(decoder_1_out6), .out7(decoder_1_out7), .sel(Fsel));
  D_Flip_Flop d_ff_1 (
    .D(multiplexer_1_out[0]), .clk(and_1_out), .Q(Dout[0]), .preset(and_9_out), .reset(and_10_out));  // open: Qn
  and and_1 (and_1_out, WE, clock_1_out);
  Clock clock_1 (.out(clock_1_out));
  D_Flip_Flop d_ff_2 (
    .D(multiplexer_1_out[1]), .clk(and_2_out), .Q(Dout[1]), .preset(and_11_out), .reset(and_12_out));  // open: Qn
  and and_2 (and_2_out, WE, clock_2_out);
  Clock clock_2 (.out(clock_2_out));
  D_Flip_Flop d_ff_3 (
    .D(multiplexer_1_out[2]), .clk(and_3_out), .Q(Dout[2]), .preset(and_13_out), .reset(and_14_out));  // open: Qn
  and and_3 (and_3_out, WE, clock_3_out);
  Clock clock_3 (.out(clock_3_out));
  D_Flip_Flop d_ff_4 (
    .D(multiplexer_1_out[3]), .clk(and_4_out), .Q(Dout[3]), .preset(and_15_out), .reset(and_16_out));  // open: Qn
  and and_4 (and_4_out, WE, clock_4_out);
  Clock clock_4 (.out(clock_4_out));
  D_Flip_Flop d_ff_5 (
    .D(multiplexer_1_out[4]), .clk(and_5_out), .Q(Dout[4]), .preset(and_17_out), .reset(and_18_out));  // open: Qn
  and and_5 (and_5_out, WE, clock_5_out);
  Clock clock_5 (.out(clock_5_out));
  D_Flip_Flop d_ff_6 (
    .D(multiplexer_1_out[5]), .clk(and_6_out), .Q(Dout[5]), .preset(and_19_out), .reset(and_20_out));  // open: Qn
  and and_6 (and_6_out, WE, clock_6_out);
  Clock clock_6 (.out(clock_6_out));
  D_Flip_Flop d_ff_7 (
    .D(multiplexer_1_out[6]), .clk(and_7_out), .Q(Dout[6]), .preset(and_21_out), .reset(and_22_out));  // open: Qn
  and and_7 (and_7_out, WE, clock_7_out);
  Clock clock_7 (.out(clock_7_out));
  D_Flip_Flop d_ff_8 (
    .D(multiplexer_1_out[7]), .clk(and_8_out), .Q(Dout[7]), .preset(and_23_out), .reset(and_24_out));  // open: Qn
  and and_8 (and_8_out, WE, clock_8_out);
  Clock clock_8 (.out(clock_8_out));
  and and_9 (and_9_out, clock_1_out, decoder_1_out0, S);
  and and_10 (and_10_out, clock_1_out, decoder_1_out0, R);
  and and_11 (and_11_out, clock_2_out, decoder_1_out1, S);
  and and_12 (and_12_out, clock_2_out, decoder_1_out1, R);
  and and_13 (and_13_out, clock_3_out, decoder_1_out2, S);
  and and_14 (and_14_out, clock_3_out, decoder_1_out2, R);
  and and_15 (and_15_out, clock_4_out, decoder_1_out3, S);
  and and_16 (and_16_out, clock_4_out, decoder_1_out3, R);
  and and_17 (and_17_out, clock_5_out, decoder_1_out4, S);
  and and_18 (and_18_out, clock_5_out, decoder_1_out4, R);
  and and_19 (and_19_out, clock_6_out, decoder_1_out5, S);
  and and_20 (and_20_out, clock_6_out, decoder_1_out5, R);
  and and_21 (and_21_out, clock_7_out, decoder_1_out6, S);
  and and_22 (and_22_out, clock_7_out, decoder_1_out6, R);
  and and_23 (and_23_out, clock_8_out, decoder_1_out7, S);
  and and_24 (and_24_out, clock_8_out, decoder_1_out7, R);
endmodule

module HA (
  input  A,
  input  B,
  output S,
  output C
);

  xor xor_1 (S, A, B);
  and and_1 (C, B, A);
endmodule

module INC (
  input  [18:0] A,
  output [18:0] S
);

  wire HA1_c, HA2_c, HA3_c, HA4_c, HA5_c, HA6_c, HA7_c, HA8_c, HA9_c, HA10_c, HA11_c, HA12_c, HA13_c, HA14_c,
       HA15_c, HA16_c, HA17_c, HA18_c;

  HA HA1 (.A(A[0]), .B(1'b1), .S(S[0]), .C(HA1_c));
  HA HA2 (.A(A[1]), .B(HA1_c), .S(S[1]), .C(HA2_c));
  HA HA3 (.A(A[2]), .B(HA2_c), .S(S[2]), .C(HA3_c));
  HA HA4 (.A(A[3]), .B(HA3_c), .S(S[3]), .C(HA4_c));
  HA HA5 (.A(A[4]), .B(HA4_c), .S(S[4]), .C(HA5_c));
  HA HA6 (.A(A[5]), .B(HA5_c), .S(S[5]), .C(HA6_c));
  HA HA7 (.A(A[6]), .B(HA6_c), .S(S[6]), .C(HA7_c));
  HA HA8 (.A(A[7]), .B(HA7_c), .S(S[7]), .C(HA8_c));
  HA HA9 (.A(A[8]), .B(HA8_c), .S(S[8]), .C(HA9_c));
  HA HA10 (.A(A[9]), .B(HA9_c), .S(S[9]), .C(HA10_c));
  HA HA11 (.A(A[10]), .B(HA10_c), .S(S[10]), .C(HA11_c));
  HA HA12 (.A(A[11]), .B(HA11_c), .S(S[11]), .C(HA12_c));
  HA HA13 (.A(A[12]), .B(HA12_c), .S(S[12]), .C(HA13_c));
  HA HA14 (.A(A[13]), .B(HA13_c), .S(S[13]), .C(HA14_c));
  HA HA15 (.A(A[14]), .B(HA14_c), .S(S[14]), .C(HA15_c));
  HA HA16 (.A(A[15]), .B(HA15_c), .S(S[15]), .C(HA16_c));
  HA HA17 (.A(A[16]), .B(HA16_c), .S(S[16]), .C(HA17_c));
  HA HA18 (.A(A[17]), .B(HA17_c), .S(S[17]), .C(HA18_c));
  HA HA19 (.A(A[18]), .B(HA18_c), .S(S[18]));  // open: C
endmodule

module PC (
  input  [19:0] Din,
  input  R,
  input  L,
  input  E,
  output [19:0] Dout
);

  wire clock_1_out, or_1_out, or_2_out;
  wire [19:0] multiplexer_1_out, multiplexer_2_out;
  wire [19:1] INC2_s;

  Multiplexer #(.width(20)) multiplexer_1 (.in0(Din), .in1(20'hffff4), .out(multiplexer_1_out), .sel(R));
  Register #(.width(20)) Program_Counter (
    .D(multiplexer_2_out), .en(or_2_out), .clk(clock_1_out), .Q(Dout), .clr(1'b0));
  Multiplexer #(.width(20)) multiplexer_2 (
    .in0({INC2_s, Dout[0]}), .in1(multiplexer_1_out), .out(multiplexer_2_out), .sel(or_1_out));
  Clock clock_1 (.out(clock_1_out));
  or or_1 (or_1_out, R, L);
  or or_2 (or_2_out, R, E);
  INC INC2 (.A(Dout[19:1]), .S(INC2_s));
endmodule

module REG_FILE (
  input  [15:0] Din,
  input  [3:0] C,
  input  [3:0] A,
  input  [3:0] B,
  input  WE,
  output [15:0] Cout,
  output [15:0] Aout,
  output [15:0] Bout,
  output [15:0] BX_Out,
  output LB,
  output [15:0] SX_Out,
  output [19:0] SP
);

  wire clock_1_out, clock_2_out, clock_3_out, clock_4_out, clock_5_out, clock_6_out, clock_7_out,
       clock_8_out, clock_9_out, clock_10_out, clock_11_out, clock_12_out, clock_13_out, clock_14_out,
       clock_15_out, demultiplexer_1_out1, demultiplexer_1_out2, demultiplexer_1_out3, demultiplexer_1_out4,
       demultiplexer_1_out5, demultiplexer_1_out6, demultiplexer_1_out7, demultiplexer_1_out8,
       demultiplexer_1_out9, demultiplexer_1_out10, demultiplexer_1_out11, demultiplexer_1_out12,
       demultiplexer_1_out13, demultiplexer_1_out14, demultiplexer_1_out15, or_1_out, or_2_out, or_3_out,
       or_4_out, or_5_out, or_6_out, or_7_out;
  wire [3:0] bit_extender_1_out;
  wire [7:0] AL, CL, DL, EL, FL;
  wire [15:8] AX, CX, DX, EX, FX;

  Demultiplexer #(.select(4)) demultiplexer_1 (
    .out1(demultiplexer_1_out1), .out2(demultiplexer_1_out2), .out3(demultiplexer_1_out3),
    .out4(demultiplexer_1_out4), .out5(demultiplexer_1_out5), .out6(demultiplexer_1_out6),
    .out7(demultiplexer_1_out7), .out8(demultiplexer_1_out8), .out9(demultiplexer_1_out9),
    .out10(demultiplexer_1_out10), .out11(demultiplexer_1_out11), .out12(demultiplexer_1_out12),
    .out13(demultiplexer_1_out13), .out14(demultiplexer_1_out14), .out15(demultiplexer_1_out15), .in(WE),
    .sel(C));  // open: out0
  Register AH (.D(Din[15:8]), .en(demultiplexer_1_out1), .clk(clock_1_out), .Q(AX), .clr(1'b0));
  Clock clock_1 (.out(clock_1_out));
  or or_1 (or_1_out, demultiplexer_1_out1, demultiplexer_1_out9);
  Register BH (.D(Din[15:8]), .en(demultiplexer_1_out2), .clk(clock_2_out), .Q(BX_Out[15:8]), .clr(1'b0));
  Clock clock_2 (.out(clock_2_out));
  or or_2 (or_2_out, demultiplexer_1_out2, demultiplexer_1_out10);
  Register CH (.D(Din[15:8]), .en(demultiplexer_1_out3), .clk(clock_3_out), .Q(CX), .clr(1'b0));
  Clock clock_3 (.out(clock_3_out));
  or or_3 (or_3_out, demultiplexer_1_out3, demultiplexer_1_out11);
  Register DH (.D(Din[15:8]), .en(demultiplexer_1_out4), .clk(clock_4_out), .Q(DX), .clr(1'b0));
  Clock clock_4 (.out(clock_4_out));
  or or_4 (or_4_out, demultiplexer_1_out4, demultiplexer_1_out12);
  Register EH (.D(Din[15:8]), .en(demultiplexer_1_out5), .clk(clock_5_out), .Q(EX), .clr(1'b0));
  Clock clock_5 (.out(clock_5_out));
  or or_5 (or_5_out, demultiplexer_1_out5, demultiplexer_1_out13);
  Register FH (.D(Din[15:8]), .en(demultiplexer_1_out6), .clk(clock_6_out), .Q(FX), .clr(1'b0));
  Clock clock_6 (.out(clock_6_out));
  or or_6 (or_6_out, demultiplexer_1_out6, demultiplexer_1_out14);
  Register SH (.D(Din[15:8]), .en(demultiplexer_1_out7), .clk(clock_7_out), .Q(SP[15:8]), .clr(1'b0));
  Clock clock_7 (.out(clock_7_out));
  or or_7 (or_7_out, demultiplexer_1_out7, demultiplexer_1_out15);
  Bit_Extender #(.in_width(16), .out_width(4), .\type ("zero")) bit_extender_1 (.in(Din), .out(bit_extender_1_out));
  Register u_AL (.D(Din[7:0]), .en(or_1_out), .clk(clock_8_out), .Q(AL), .clr(1'b0));
  Clock clock_8 (.out(clock_8_out));
  Register BL (.D(Din[7:0]), .en(or_2_out), .clk(clock_9_out), .Q(BX_Out[7:0]), .clr(1'b0));
  Clock clock_9 (.out(clock_9_out));
  Register u_CL (.D(Din[7:0]), .en(or_3_out), .clk(clock_10_out), .Q(CL), .clr(1'b0));
  Clock clock_10 (.out(clock_10_out));
  Register u_DL (.D(Din[7:0]), .en(or_4_out), .clk(clock_11_out), .Q(DL), .clr(1'b0));
  Clock clock_11 (.out(clock_11_out));
  Register u_EL (.D(Din[7:0]), .en(or_5_out), .clk(clock_12_out), .Q(EL), .clr(1'b0));
  Clock clock_12 (.out(clock_12_out));
  Register u_FL (.D(Din[7:0]), .en(or_6_out), .clk(clock_13_out), .Q(FL), .clr(1'b0));
  Clock clock_13 (.out(clock_13_out));
  Register SL (.D(Din[7:0]), .en(or_7_out), .clk(clock_14_out), .Q(SP[7:0]), .clr(1'b0));
  Clock clock_14 (.out(clock_14_out));
  Register #(.width(4)) SY (
    .D(bit_extender_1_out), .en(demultiplexer_1_out8), .clk(clock_15_out), .Q(SP[19:16]), .clr(1'b0));
  Clock clock_15 (.out(clock_15_out));
  Multiplexer #(.select(4), .width(16)) multiplexer_1 (
    .in0({16{1'b0}}), .in1({AX, AL}), .in2(BX_Out), .in3({CX, CL}), .in4({DX, DL}), .in5({EX, EL}),
    .in6({FX, FL}), .in7(SP[15:0]), .in8({{12{1'b0}}, SP[19:16]}), .in9({{8{1'b0}}, AL}),
    .in10({{8{1'b0}}, BX_Out[7:0]}), .in11({{8{1'b0}}, CL}), .in12({{8{1'b0}}, DL}), .in13({{8{1'b0}}, EL}),
    .in14({{8{1'b0}}, FL}), .in15({{8{1'b0}}, SP[7:0]}), .out(Cout), .sel(C));
  Multiplexer #(.select(4), .width(16)) multiplexer_2 (
    .in0({16{1'b0}}), .in1({AX, AL}), .in2(BX_Out), .in3({CX, CL}), .in4({DX, DL}), .in5({EX, EL}),
    .in6({FX, FL}), .in7(SP[15:0]), .in8({{12{1'b0}}, SP[19:16]}), .in9({{8{1'b0}}, AL}),
    .in10({{8{1'b0}}, BX_Out[7:0]}), .in11({{8{1'b0}}, CL}), .in12({{8{1'b0}}, DL}), .in13({{8{1'b0}}, EL}),
    .in14({{8{1'b0}}, FL}), .in15({{8{1'b0}}, SP[7:0]}), .out(Aout), .sel(A));
  Multiplexer #(.select(4), .width(16)) multiplexer_3 (
    .in0({16{1'b0}}), .in1({AX, AL}), .in2(BX_Out), .in3({CX, CL}), .in4({DX, DL}), .in5({EX, EL}),
    .in6({FX, FL}), .in7(SP[15:0]), .in8({{12{1'b0}}, SP[19:16]}), .in9({{8{1'b0}}, AL}),
    .in10({{8{1'b0}}, BX_Out[7:0]}), .in11({{8{1'b0}}, CL}), .in12({{8{1'b0}}, DL}), .in13({{8{1'b0}}, EL}),
    .in14({{8{1'b0}}, FL}), .in15({{8{1'b0}}, SP[7:0]}), .out(Bout), .sel(B));
  PLA #(.in_width(4), .out_width(1), .\table ("1001 1 # AL\n1010 1 # BL\n1011 1 # CL\n1100 1 # DL\n1101 1 # EL\n1110 1 # FL\n1111 1 # SL")) LOW (
    .in(C), .out(LB));

  assign SX_Out = SP[15:0];

  // Other names for the same wires on the sheet: AX[7:0] = AL; BL[7:0] = BX_Out[7:0]; BX[15:0] = BX_Out; CX[7:0] = CL;
  //   DX[7:0] = DL; EX[7:0] = EL; FX[7:0] = FL; SL[7:0] = SP[7:0]; SX[15:0] = SP[15:0]; SY[3:0] = SP[19:16]
endmodule
