// Logisim project SRM1_TEST_MACHINE.circ as structural Verilog: 1 circuit, main circuit main
module main (
  input  RDY
);

  wire and_1_out, and_2_out, and_3_out, clock_3_out, clock_4_out, clock_5_out, demultiplexer_1_out0,
       demultiplexer_1_out1, F, IRQ, keyboard_1_avail, not_1_out, not_2_out, not_3_out, ram_1_p5, ram_2_p5,
       RES, RW, TW, WS;
  wire [3:0] AS;
  wire [6:0] keyboard_1_data;
  wire [7:0] DH, srm1_1_dli;
  wire [15:0] AB, key, multiplexer_1_out, RAM1, RAM2, ROM1;

  Multiplexer #(.select(4), .width(16)) multiplexer_1 (
    .in0(RAM1), .in1(RAM2), .in2(key), .in15(ROM1), .out(multiplexer_1_out), .sel(AS));  // open: in3, in4, in5, in6, in7, in8, in9, in10, in11, in12, in13, in14
  SRM1 srm1_1 (
    .DLO(multiplexer_1_out[7:0]), .DHO(multiplexer_1_out[15:8]), .RES(RES), .RDY(RDY), .IRQ(IRQ), .NMI(1'b0),
    .AB({AS, AB}), .DHI(DH), .DLI(srm1_1_dli), .RW(RW), .WS(WS), .Interrupt_Fetch(F));  // open: ML
  Demultiplexer #(.select(4)) demultiplexer_1 (
    .out0(demultiplexer_1_out0), .out1(demultiplexer_1_out1), .out2(TW), .in(RW), .sel(AS));  // open: out3, out4, out5, out6, out7, out8, out9, out10, out11, out12, out13, out14, out15
  // RAM #(.addrWidth(16), .enables("line"), .line("dual"), .misaligned("true")) ram_1: pin names not known; wires that end beside it: AB, demultiplexer_1_out0, 1'b1, WS, ram_1_p5, DH, srm1_1_dli, RAM1[15:8], RAM1[7:0]
  Clock clock_1 (.out(ram_1_p5));
  // RAM #(.addrWidth(16), .enables("line"), .line("dual"), .misaligned("true")) ram_2: pin names not known; wires that end beside it: AB, demultiplexer_1_out1, 1'b1, WS, ram_2_p5, DH, srm1_1_dli, RAM2[15:8], RAM2[7:0]
  Clock clock_2 (.out(ram_2_p5));
  // ROM #(.addrWidth(16), .line("dual"), .misaligned("true")) rom_1: pin names not known; wires that end beside it: AB, ROM1[15:8], ROM1[7:0]
  Clock clock_3 (.out(clock_3_out));
  TTY tty_1 (.data(DH[6:0]), .clk(clock_3_out), .we(TW));  // open: clr
  Clock clock_4 (.out(clock_4_out));
  Keyboard #(.buflen(1)) keyboard_1 (
    .clk(clock_4_out), .re(and_1_out), .avail(keyboard_1_avail), .data(keyboard_1_data));  // open: clr
  and and_1 (and_1_out, and_2_out, ~RW);  // AND_Gate
  and and_2 (and_2_out, ~AS[3], AS[2], ~AS[1], ~AS[0]);  // AND_Gate
  not not_1 (not_1_out, keyboard_1_avail);
  not not_2 (not_2_out, not_1_out);
  not not_3 (not_3_out, not_2_out);
  and and_3 (and_3_out, not_3_out, keyboard_1_avail);
  S_R_Flip_Flop s_r_ff_1 (.S(1'b0), .R(F), .clk(clock_5_out), .Q(IRQ), .reset(1'b0), .preset(and_3_out));  // open: Qn
  Clock clock_5 (.out(clock_5_out));
  assign key = {{9{1'b0}}, keyboard_1_data};  // Bit_Extender bit_extender_1

  // Notes on the sheet:
  //   RDY: initial=0x1
  //   contents of rom_1 (hex, n*v repeats v):
  //   48 65 6c 6c 6f 20 57 6f 72 6c 64 21 a 0 30 20 0 0 51 9f 0 0 32 90 0 0 90 f 0 2a 40 92 0 0 30 22 0 1
  //   80 f 0 12 80 f 0 2a 65478*0 80 f 0 e
endmodule
